# Fritzing sketch 4_WebGuiTest (saved by Fritzing 0.9.2b)
breadboards: 1

parts:
  Part1 = Intel Edison Arduinobreakout
  RE1 = Rotary Encoder [package=THT]
  R1 = Rotary Potentiometer (Small) [maximum_resistance=100kΩ package=THT]
  S1 = Pushbutton [package="[THT]"]

nets:
  N1: Part1.A0, R1.wiper
  N2: Part1.D5_PWM, S1.Pin_3, S1.Pin_4
  N3: Part1.D6_PWM, RE1.EncoderPinA
  N4: Part1.D7, RE1.EncoderPinB
  N5: Part1.5V, R1.leg1
  N6: Part1.GND, RE1.EncoderPinC, R1.leg2, S1.Pin_1, S1.Pin_2
